# Fritzing sketch L293B-with-two-motors-version3 (saved by Fritzing 0.7.11b)
breadboards: 1

parts:
  D1 = Rectifier Diode [part_number=1N4001 package="300 mil [THT]"]
  D2 = Rectifier Diode [part_number=1N4001 package="300 mil [THT]"]
  D3 = Rectifier Diode [part_number=1N4001 package="300 mil [THT]"]
  D4 = Rectifier Diode [part_number=1N4001 package="300 mil [THT]"]
  M1 = DC Motor
  IC1 = L293D [package=THT]

nets:
  N1: D1.cathode, D2.cathode
  N2: D1.anode, D3.cathode, M1.pin_1, IC1.Out_2_(_Controlled_by_Enable_1_)
  N3: D2.anode, D4.cathode, M1.pin_2, IC1.Out_1_(_Controlled_by_Enable_1_)
  N4: D3.anode, D4.anode, IC1.0V
